// Logisim project alu.circ as structural Verilog: 24 circuits, main circuit main2
module main2 (
  input  [31:0] A,
  input  [31:0] B,
  input  [3:0] ALUSel,
  output [31:0] Result,
  output Zero,
  output OverFlow
);

  wire adder_1_cout, and_1_out, and_2_out, and_3_out, and_4_out, and_5_out, and_6_out, and_7_out, and_8_out,
       and_9_out, and_10_out, and_11_out, and_12_out, and_13_out, and_14_out, and_15_out, and_16_out,
       not_1_out, not_2_out, not_3_out, not_4_out, not_5_out, not_6_out, not_7_out, not_8_out, not_9_out,
       not_10_out, not_11_out, not_12_out, not_13_out, not_14_out, not_15_out, not_16_out, not_17_out,
       not_18_out, not_19_out, not_20_out, not_21_out, not_22_out, not_23_out, not_24_out, not_25_out,
       not_26_out, not_27_out, not_28_out, not_29_out, not_30_out, not_31_out, not_32_out, or_3_out;
  wire [31:0] adder_1_out, and_17_out_3, bsel_1_result, l_32and1_597dd26d_1_out_3, l_32and1_597dd26d_2_out_3,
       l_32and1_597dd26d_3_out_3, l_32and1_597dd26d_4_out_3, l_32and1_597dd26d_5_out_3,
       l_32and1_597dd26d_6_out_3, l_32and1_597dd26d_7_out_3, l_32and1_597dd26d_8_out_3,
       l_32and1_597dd26d_9_out_3, l_32and1_597dd26d_11_out_3, l_32and1_597dd26d_12_out_3,
       l_32and1_597dd26d_13_out_3, l_32and1_597dd26d_14_out_3, l_32and1_597dd26d_15_out_3, mul_1_out_3,
       mulh_1_result, mulhu_1_result, or_1_result, sll_1_out_3, slt_1_out_3, sltu_1_out_3, sra_1_out_3,
       srl_1_out_3, subtractor_1_out, xor_1_result;

  Adder #(.width(32)) adder_1 (.a(A), .b(B), .out(adder_1_out), .cout(adder_1_cout));  // open: cin
  sll sll_1 (.in_1(A), .in_2(B), .out_3(sll_1_out_3));
  slt slt_1 (.in_1(A), .in_2(B), .out_3(slt_1_out_3));
  not not_1 (not_1_out, ALUSel[0]);
  not not_2 (not_2_out, ALUSel[1]);
  not not_3 (not_3_out, ALUSel[2]);
  not not_4 (not_4_out, ALUSel[3]);
  not not_5 (not_5_out, ALUSel[1]);
  not not_6 (not_6_out, ALUSel[2]);
  not not_7 (not_7_out, ALUSel[3]);
  not not_8 (not_8_out, ALUSel[0]);
  not not_9 (not_9_out, ALUSel[2]);
  not not_10 (not_10_out, ALUSel[3]);
  not not_11 (not_11_out, ALUSel[2]);
  not not_12 (not_12_out, ALUSel[3]);
  not not_13 (not_13_out, ALUSel[0]);
  not not_14 (not_14_out, ALUSel[1]);
  not not_15 (not_15_out, ALUSel[3]);
  not not_16 (not_16_out, ALUSel[1]);
  not not_17 (not_17_out, ALUSel[3]);
  not not_18 (not_18_out, ALUSel[0]);
  not not_19 (not_19_out, ALUSel[3]);
  not not_20 (not_20_out, ALUSel[3]);
  not not_21 (not_21_out, ALUSel[0]);
  not not_22 (not_22_out, ALUSel[1]);
  not not_23 (not_23_out, ALUSel[2]);
  not not_24 (not_24_out, ALUSel[1]);
  not not_25 (not_25_out, ALUSel[2]);
  not not_26 (not_26_out, ALUSel[0]);
  not not_27 (not_27_out, ALUSel[2]);
  not not_28 (not_28_out, ALUSel[2]);
  not not_29 (not_29_out, ALUSel[0]);
  not not_30 (not_30_out, ALUSel[1]);
  not not_31 (not_31_out, ALUSel[1]);
  not not_32 (not_32_out, ALUSel[0]);
  sltu sltu_1 (.in_1(A), .in_2(B), .out_3(sltu_1_out_3));
  and and_1 (and_1_out, not_1_out, not_2_out, not_3_out, not_4_out);
  and and_2 (and_2_out, ALUSel[0], not_5_out, not_6_out, not_7_out);
  and and_3 (and_3_out, not_8_out, ALUSel[1], not_9_out, not_10_out);
  and and_4 (and_4_out, ALUSel[0], ALUSel[1], not_11_out, not_12_out);
  and and_5 (and_5_out, not_13_out, not_14_out, ALUSel[2], not_15_out);
  and and_6 (and_6_out, ALUSel[0], not_16_out, ALUSel[2], not_17_out);
  and and_7 (and_7_out, not_18_out, ALUSel[1], ALUSel[2], not_19_out);
  and and_8 (and_8_out, ALUSel[0], ALUSel[1], ALUSel[2], not_20_out);
  and and_9 (and_9_out, not_21_out, not_22_out, not_23_out, ALUSel[3]);
  and and_10 (and_10_out, ALUSel[0], not_24_out, not_25_out, ALUSel[3]);
  and and_11 (and_11_out, not_26_out, ALUSel[1], not_27_out, ALUSel[3]);
  and and_12 (and_12_out, ALUSel[0], ALUSel[1], not_28_out, ALUSel[3]);
  and and_13 (and_13_out, not_29_out, not_30_out, ALUSel[2], ALUSel[3]);
  and and_14 (and_14_out, ALUSel[0], not_31_out, ALUSel[2], ALUSel[3]);
  and and_15 (and_15_out, not_32_out, ALUSel[1], ALUSel[2], ALUSel[3]);
  and and_16 (and_16_out, ALUSel[0], ALUSel[1], ALUSel[2], ALUSel[3]);
  \xor  xor_1 (.A(B), .B(A), .Result(xor_1_result));
  L_32and1_597dd26d l_32and1_597dd26d_1 (.in_1(adder_1_out), .in_2(and_1_out), .out_3(l_32and1_597dd26d_1_out_3));
  L_32and1_597dd26d l_32and1_597dd26d_2 (.in_1(sll_1_out_3), .in_2(and_2_out), .out_3(l_32and1_597dd26d_2_out_3));
  L_32and1_597dd26d l_32and1_597dd26d_3 (.in_1(xor_1_result), .in_2(and_5_out), .out_3(l_32and1_597dd26d_3_out_3));
  L_32and1_597dd26d l_32and1_597dd26d_4 (.in_1(slt_1_out_3), .in_2(and_3_out), .out_3(l_32and1_597dd26d_4_out_3));
  L_32and1_597dd26d l_32and1_597dd26d_5 (.in_1(sltu_1_out_3), .in_2(and_4_out), .out_3(l_32and1_597dd26d_5_out_3));
  srl srl_1 (.in_1(A), .in_2(B), .out_3(srl_1_out_3));
  \or  or_1 (.A(B), .B(A), .Result(or_1_result));
  L_32and1_597dd26d l_32and1_597dd26d_6 (.in_1(srl_1_out_3), .in_2(and_6_out), .out_3(l_32and1_597dd26d_6_out_3));
  \and  and_17 (.in_1(B), .in_2(A), .out_3(and_17_out_3));
  L_32and1_597dd26d l_32and1_597dd26d_7 (.in_1(or_1_result), .in_2(and_7_out), .out_3(l_32and1_597dd26d_7_out_3));
  mul mul_1 (.in_1(B), .in_2(A), .out_3(mul_1_out_3));
  L_32and1_597dd26d l_32and1_597dd26d_8 (.in_1(and_17_out_3), .in_2(and_8_out), .out_3(l_32and1_597dd26d_8_out_3));
  L_32and1_597dd26d l_32and1_597dd26d_9 (.in_1(mul_1_out_3), .in_2(and_9_out), .out_3(l_32and1_597dd26d_9_out_3));
  mulh mulh_1 (.A(A), .B(B), .Result(mulh_1_result));
  L_32and1_597dd26d l_32and1_597dd26d_10 ();  // open: in_1, in_2, out_3
  L_32and1_597dd26d l_32and1_597dd26d_11 (.in_1(mulh_1_result), .in_2(and_10_out), .out_3(l_32and1_597dd26d_11_out_3));
  mulhu mulhu_1 (.A(A), .B(B), .Result(mulhu_1_result));
  Subtractor #(.width(32)) subtractor_1 (.a(A), .b(B), .out(subtractor_1_out));  // open: bin, bout
  L_32and1_597dd26d l_32and1_597dd26d_12 (.in_1(mulhu_1_result), .in_2(and_12_out), .out_3(l_32and1_597dd26d_12_out_3));
  L_32and1_597dd26d l_32and1_597dd26d_13 (
    .in_1(subtractor_1_out), .in_2(and_13_out), .out_3(l_32and1_597dd26d_13_out_3));
  sra sra_1 (.in_1(A), .in_2(B), .out_3(sra_1_out_3));
  L_32and1_597dd26d l_32and1_597dd26d_14 (.in_1(sra_1_out_3), .in_2(and_14_out), .out_3(l_32and1_597dd26d_14_out_3));
  bsel bsel_1 (.B(B), .Result(bsel_1_result));
  L_32and1_597dd26d l_32and1_597dd26d_15 (.in_1(bsel_1_result), .in_2(and_16_out), .out_3(l_32and1_597dd26d_15_out_3));
  and and_18 (OverFlow, adder_1_cout, and_1_out);
  assign Result = l_32and1_597dd26d_1_out_3 | l_32and1_597dd26d_2_out_3 | l_32and1_597dd26d_4_out_3 | l_32and1_597dd26d_5_out_3 | l_32and1_597dd26d_3_out_3 | l_32and1_597dd26d_6_out_3 | l_32and1_597dd26d_7_out_3 | l_32and1_597dd26d_8_out_3 | l_32and1_597dd26d_9_out_3 | l_32and1_597dd26d_11_out_3 | l_32and1_597dd26d_12_out_3 | l_32and1_597dd26d_13_out_3 | l_32and1_597dd26d_14_out_3 | l_32and1_597dd26d_15_out_3;  // OR_Gate or_2, 32 bits wide
  or or_3 (or_3_out, Result[0], Result[1], Result[2], Result[3], Result[4], Result[5], Result[6], Result[7], Result[8], Result[9], Result[10], Result[11], Result[12], Result[13], Result[14], Result[15], Result[17], Result[18], Result[19], Result[20], Result[21], Result[22], Result[23], Result[24], Result[25], Result[26], Result[27], Result[28], Result[29], Result[30], Result[31], Result[16]);
  not not_33 (Zero, or_3_out);
endmodule

module sll (
  input  [31:0] in_1,
  input  [31:0] in_2,
  output [31:0] out_3
);

  wire not_1_out, or_1_out;
  wire [31:0] shifter_1_out;

  Shifter #(.width(32)) shifter_1 (.in(in_1), .\dist (in_2[4:0]), .out(shifter_1_out));
  or or_1 (or_1_out, in_2[5], in_2[6], in_2[7], in_2[8], in_2[9], in_2[10], in_2[11], in_2[12], in_2[13], in_2[14], in_2[15], in_2[16], in_2[17], in_2[18], in_2[19], in_2[20], in_2[21], in_2[22], in_2[23], in_2[24], in_2[25], in_2[26], in_2[27], in_2[28], in_2[29], in_2[30], in_2[31]);
  L_32and1_597dd26d l_32and1_597dd26d_1 (.in_1(shifter_1_out), .in_2(not_1_out), .out_3(out_3));
  not not_1 (not_1_out, or_1_out);
endmodule

module \xor  (
  input  [31:0] A,
  input  [31:0] B,
  output [31:0] Result
);

  assign Result = A ^ B;  // XOR_Gate xor_1, 32 bits wide
endmodule

module \and  (
  input  [31:0] in_1,
  input  [31:0] in_2,
  output [31:0] out_3
);

  assign out_3 = in_1 & in_2;  // AND_Gate and_1, 32 bits wide
endmodule

module \or  (
  input  [31:0] A,
  input  [31:0] B,
  output [31:0] Result
);

  assign Result = A | B;  // OR_Gate or_1, 32 bits wide
endmodule

module srl (
  input  [31:0] in_1,
  input  [31:0] in_2,
  output [31:0] out_3
);

  wire not_1_out, or_1_out;
  wire [31:0] shifter_1_out;

  Shifter #(.shift("lr"), .width(32)) shifter_1 (.in(in_1), .\dist (in_2[4:0]), .out(shifter_1_out));
  or or_1 (or_1_out, in_2[5], in_2[6], in_2[7], in_2[8], in_2[9], in_2[10], in_2[11], in_2[12], in_2[13], in_2[14], in_2[15], in_2[16], in_2[17], in_2[18], in_2[19], in_2[20], in_2[21], in_2[22], in_2[23], in_2[24], in_2[25], in_2[26], in_2[27], in_2[28], in_2[29], in_2[30], in_2[31]);
  not not_1 (not_1_out, or_1_out);
  L_32and1_597dd26d l_32and1_597dd26d_1 (.in_1(shifter_1_out), .in_2(not_1_out), .out_3(out_3));
endmodule

module sra (
  input  [31:0] in_1,
  input  [31:0] in_2,
  output [31:0] out_3
);

  wire or_1_out;
  wire [31:0] shifter_1_out;

  Shifter #(.shift("ar"), .width(32)) shifter_1 (.in(in_1), .\dist (in_2[4:0]), .out(shifter_1_out));
  or or_1 (or_1_out, in_2[5], in_2[6], in_2[7], in_2[8], in_2[9], in_2[10], in_2[11], in_2[12], in_2[13], in_2[14], in_2[15], in_2[16], in_2[17], in_2[18], in_2[19], in_2[20], in_2[21], in_2[22], in_2[23], in_2[24], in_2[25], in_2[26], in_2[27], in_2[28], in_2[29], in_2[30], in_2[31]);
  L_32or1_828f0ab1 l_32or1_828f0ab1_1 (.in_1(shifter_1_out), .in_2(or_1_out), .out_3(out_3));
endmodule

module bsel (
  input  [31:0] B,
  output [31:0] Result
);


  assign Result = B;
endmodule

module L_32or1_828f0ab1 (
  input  [31:0] in_1,
  input  in_2,
  output [31:0] out_3
);

  assign out_3 = in_1 | {32{in_2}};  // OR_Gate or_1, 32 bits wide
endmodule

module L_32and1_597dd26d (
  input  [31:0] in_1,
  input  in_2,
  output [31:0] out_3
);

  assign out_3 = in_1 & {32{in_2}};  // AND_Gate and_1, 32 bits wide
endmodule

module mul (
  input  [31:0] in_1,
  input  [31:0] in_2,
  output [31:0] out_3
);

  Multiplier #(.width(32)) multiplier_1 (.a(in_1), .b(in_2), .out(out_3));  // open: cin, cout
endmodule

module L_32to31_82463699 (
  input  [31:0] in_1,
  output [30:0] out_2,
  output out_3
);


  assign out_2 = in_1[30:0];
  assign out_3 = in_1[31];
endmodule

module L_31to32_3c6b2aeb (
  input  [30:0] in_1,
  input  in_2,
  output [31:0] out_3
);


  assign out_3 = {in_2, in_1};
endmodule

module slt (
  input  [31:0] in_1,
  input  [31:0] in_2,
  output [31:0] out_3
);

  wire comparator_1_eq, comparator_1_gt, comparator_1_lt, not_1_out, not_2_out;

  Comparator #(.width(32)) comparator_1 (
    .a(in_1), .b(in_2), .gt(comparator_1_gt), .eq(comparator_1_eq), .lt(comparator_1_lt));
  not not_1 (not_1_out, comparator_1_gt);
  not not_2 (not_2_out, comparator_1_eq);
  and and_1 (out_3[0], not_1_out, not_2_out, comparator_1_lt);

  assign out_3[31:1] = {31{1'b0}};
endmodule

module Adder2 (
  input  [31:0] in_1,
  input  [31:0] in_2,
  output [31:0] out_3,
  output out_4
);

  wire and_1_out, and_2_out, and_3_out, l_32to31_82463699_1_out_3, l_32to31_82463699_2_out_3,
       l_32to31_82463699_3_out_3, xor_1_out, xor_2_out;
  wire [30:0] l_32to31_82463699_1_out_2, l_32to31_82463699_2_out_2, l_32to31_82463699_3_out_2;
  wire [31:0] adder_1_out, l_31to32_3c6b2aeb_1_out_3, l_31to32_3c6b2aeb_2_out_3;

  L_32to31_82463699 l_32to31_82463699_1 (
    .in_1(in_1), .out_2(l_32to31_82463699_1_out_2), .out_3(l_32to31_82463699_1_out_3));
  L_32to31_82463699 l_32to31_82463699_2 (
    .in_1(in_2), .out_2(l_32to31_82463699_2_out_2), .out_3(l_32to31_82463699_2_out_3));
  L_31to32_3c6b2aeb l_31to32_3c6b2aeb_1 (
    .in_1(l_32to31_82463699_1_out_2), .in_2(1'b0), .out_3(l_31to32_3c6b2aeb_1_out_3));
  L_31to32_3c6b2aeb l_31to32_3c6b2aeb_2 (
    .in_1(l_32to31_82463699_2_out_2), .in_2(1'b0), .out_3(l_31to32_3c6b2aeb_2_out_3));
  Adder #(.width(32)) adder_1 (
    .a(l_31to32_3c6b2aeb_1_out_3), .b(l_31to32_3c6b2aeb_2_out_3), .out(adder_1_out));  // open: cin, cout
  L_32to31_82463699 l_32to31_82463699_3 (
    .in_1(adder_1_out), .out_2(l_32to31_82463699_3_out_2), .out_3(l_32to31_82463699_3_out_3));
  and and_1 (and_1_out, l_32to31_82463699_3_out_3, l_32to31_82463699_1_out_3);
  and and_2 (and_2_out, l_32to31_82463699_1_out_3, l_32to31_82463699_2_out_3);
  and and_3 (and_3_out, l_32to31_82463699_3_out_3, l_32to31_82463699_2_out_3);
  xor xor_1 (xor_1_out, l_32to31_82463699_3_out_3, l_32to31_82463699_1_out_3);
  xor xor_2 (xor_2_out, xor_1_out, l_32to31_82463699_2_out_3);
  or or_1 (out_4, and_1_out, and_2_out, and_3_out);
  L_31to32_3c6b2aeb l_31to32_3c6b2aeb_3 (.in_1(l_32to31_82463699_3_out_2), .in_2(xor_2_out), .out_3(out_3));
endmodule

module Sub_new (
  input  [31:0] in_1,
  input  [31:0] in_2,
  output [31:0] out_3
);

  wire l_32to31_82463699_1_out_3, l_32to31_82463699_2_out_3, l_32to31_82463699_3_out_3, xor_1_out, xor_2_out;
  wire [30:0] l_32to31_82463699_1_out_2, l_32to31_82463699_2_out_2, l_32to31_82463699_3_out_2;
  wire [31:0] adder_1_out, l_31to32_3c6b2aeb_1_out_3, l_31to32_3c6b2aeb_2_out_3, negator_1_out;

  Negator #(.width(32)) negator_1 (.in(in_2), .out(negator_1_out));
  L_32to31_82463699 l_32to31_82463699_1 (
    .in_1(in_1), .out_2(l_32to31_82463699_1_out_2), .out_3(l_32to31_82463699_1_out_3));
  L_32to31_82463699 l_32to31_82463699_2 (
    .in_1(negator_1_out), .out_2(l_32to31_82463699_2_out_2), .out_3(l_32to31_82463699_2_out_3));
  L_31to32_3c6b2aeb l_31to32_3c6b2aeb_1 (
    .in_1(l_32to31_82463699_1_out_2), .in_2(1'b0), .out_3(l_31to32_3c6b2aeb_1_out_3));
  L_31to32_3c6b2aeb l_31to32_3c6b2aeb_2 (
    .in_1(l_32to31_82463699_2_out_2), .in_2(1'b0), .out_3(l_31to32_3c6b2aeb_2_out_3));
  Adder #(.width(32)) adder_1 (
    .a(l_31to32_3c6b2aeb_1_out_3), .b(l_31to32_3c6b2aeb_2_out_3), .out(adder_1_out));  // open: cin, cout
  L_32to31_82463699 l_32to31_82463699_3 (
    .in_1(adder_1_out), .out_2(l_32to31_82463699_3_out_2), .out_3(l_32to31_82463699_3_out_3));
  xor xor_1 (xor_1_out, l_32to31_82463699_3_out_3, l_32to31_82463699_1_out_3);
  xor xor_2 (xor_2_out, xor_1_out, l_32to31_82463699_2_out_3);
  L_31to32_3c6b2aeb l_31to32_3c6b2aeb_3 (.in_1(l_32to31_82463699_3_out_2), .in_2(xor_2_out), .out_3(out_3));
endmodule

module Sele_32 (
  input  [31:0] in_1,
  input  in_2,
  output [31:0] out_3
);

  assign out_3 = in_1 & {32{in_2}};  // AND_Gate and_1, 32 bits wide
endmodule

module magnitude (
  input  [31:0] in_1,
  input  [31:0] in_2,
  output out_3
);

  wire and_1_out, and_2_out, and_3_out, and_4_out, and_5_out, and_6_out, and_7_out, and_8_out, and_9_out,
       and_10_out, and_11_out, comparator_1_eq, comparator_1_gt, l_32to31_82463699_1_out_3,
       l_32to31_82463699_2_out_3, not_1_out, not_2_out, not_3_out, not_4_out, not_5_out, not_6_out,
       not_7_out, not_8_out, not_9_out, or_1_out;
  wire [30:0] l_32to31_82463699_1_out_2, l_32to31_82463699_2_out_2;
  wire [31:0] adder2_1_out_3, adder2_2_out_3, l_31to32_3c6b2aeb_1_out_3, l_31to32_3c6b2aeb_2_out_3,
       negator_1_out, negator_2_out, sele_32_1_out_3, sele_32_2_out_3, sele_32_3_out_3, sele_32_4_out_3;

  L_32to31_82463699 l_32to31_82463699_1 (
    .in_1(in_2), .out_2(l_32to31_82463699_1_out_2), .out_3(l_32to31_82463699_1_out_3));
  L_31to32_3c6b2aeb l_31to32_3c6b2aeb_1 (
    .in_1(l_32to31_82463699_1_out_2), .in_2(l_32to31_82463699_1_out_3), .out_3(l_31to32_3c6b2aeb_1_out_3));
  L_32to31_82463699 l_32to31_82463699_2 (
    .in_1(in_1), .out_2(l_32to31_82463699_2_out_2), .out_3(l_32to31_82463699_2_out_3));
  L_31to32_3c6b2aeb l_31to32_3c6b2aeb_2 (
    .in_1(l_32to31_82463699_2_out_2), .in_2(l_32to31_82463699_2_out_3), .out_3(l_31to32_3c6b2aeb_2_out_3));
  Negator #(.width(32)) negator_1 (.in(l_31to32_3c6b2aeb_2_out_3), .out(negator_1_out));
  Negator #(.width(32)) negator_2 (.in(l_31to32_3c6b2aeb_1_out_3), .out(negator_2_out));
  not not_1 (not_1_out, l_32to31_82463699_2_out_3);
  not not_2 (not_2_out, l_32to31_82463699_1_out_3);
  Sele_32 sele_32_1 (.in_1(l_31to32_3c6b2aeb_2_out_3), .in_2(not_1_out), .out_3(sele_32_1_out_3));
  Sele_32 sele_32_2 (.in_1(negator_1_out), .in_2(l_32to31_82463699_2_out_3), .out_3(sele_32_2_out_3));
  Sele_32 sele_32_3 (.in_1(l_31to32_3c6b2aeb_1_out_3), .in_2(not_2_out), .out_3(sele_32_3_out_3));
  Sele_32 sele_32_4 (.in_1(negator_2_out), .in_2(l_32to31_82463699_1_out_3), .out_3(sele_32_4_out_3));
  Adder2 adder2_1 (.in_1(sele_32_1_out_3), .in_2(sele_32_2_out_3), .out_3(adder2_1_out_3));  // open: out_4
  Adder2 adder2_2 (.in_1(sele_32_3_out_3), .in_2(sele_32_4_out_3), .out_3(adder2_2_out_3));  // open: out_4
  Comparator #(.mode("unsigned"), .width(32)) comparator_1 (
    .a(adder2_1_out_3), .b(adder2_2_out_3), .gt(comparator_1_gt), .eq(comparator_1_eq));  // open: lt
  not not_3 (not_3_out, l_32to31_82463699_1_out_3);
  not not_4 (not_4_out, comparator_1_gt);
  not not_5 (not_5_out, l_32to31_82463699_2_out_3);
  not not_6 (not_6_out, l_32to31_82463699_1_out_3);
  not not_7 (not_7_out, l_32to31_82463699_2_out_3);
  not not_8 (not_8_out, l_32to31_82463699_1_out_3);
  and and_1 (and_1_out, l_32to31_82463699_2_out_3, comparator_1_gt);
  and and_2 (and_2_out, not_3_out, not_4_out);
  not not_9 (not_9_out, comparator_1_eq);
  and and_3 (and_3_out, l_32to31_82463699_2_out_3, comparator_1_eq, l_32to31_82463699_1_out_3);
  and and_4 (and_4_out, not_5_out, comparator_1_eq, not_6_out);
  and and_5 (and_5_out, comparator_1_eq, l_32to31_82463699_1_out_3, not_7_out);
  and and_6 (and_6_out, comparator_1_eq, l_32to31_82463699_2_out_3, not_8_out);
  or or_1 (or_1_out, and_1_out, and_2_out);
  and and_7 (and_7_out, or_1_out, not_9_out);
  and and_8 (and_8_out, and_3_out, 1'b0);
  and and_9 (and_9_out, and_4_out, 1'b0);
  and and_10 (and_10_out, l_32to31_82463699_2_out_3, and_5_out);
  and and_11 (and_11_out, l_32to31_82463699_2_out_3, and_6_out);
  or or_2 (out_3, and_7_out, and_8_out, and_9_out, and_10_out, and_11_out);
endmodule

module mulh (
  input  [31:0] A,
  input  [31:0] B,
  output [31:0] Result
);

  Multiplier #(.width(32)) multiplier_1 (.a(A), .b(B), .cout(Result));  // open: out, cin
endmodule

module Add_new (
  input  [31:0] A,
  input  [31:0] B,
  output [31:0] Result,
  output Overflow
);

  wire l_32to31_82463699_1_out_3, l_32to31_82463699_2_out_3, l_32to31_82463699_3_out_3, xor_1_out, xor_2_out;
  wire [30:0] l_32to31_82463699_1_out_2, l_32to31_82463699_2_out_2, l_32to31_82463699_3_out_2;
  wire [31:0] adder_1_out, l_31to32_3c6b2aeb_1_out_3, l_31to32_3c6b2aeb_2_out_3;

  L_32to31_82463699 l_32to31_82463699_1 (
    .in_1(A), .out_2(l_32to31_82463699_1_out_2), .out_3(l_32to31_82463699_1_out_3));
  L_32to31_82463699 l_32to31_82463699_2 (
    .in_1(B), .out_2(l_32to31_82463699_2_out_2), .out_3(l_32to31_82463699_2_out_3));
  L_31to32_3c6b2aeb l_31to32_3c6b2aeb_1 (
    .in_1(l_32to31_82463699_1_out_2), .in_2(1'b0), .out_3(l_31to32_3c6b2aeb_1_out_3));
  L_31to32_3c6b2aeb l_31to32_3c6b2aeb_2 (
    .in_1(l_32to31_82463699_2_out_2), .in_2(1'b0), .out_3(l_31to32_3c6b2aeb_2_out_3));
  Adder #(.width(32)) adder_1 (
    .a(l_31to32_3c6b2aeb_1_out_3), .b(l_31to32_3c6b2aeb_2_out_3), .out(adder_1_out));  // open: cin, cout
  L_32to31_82463699 l_32to31_82463699_3 (
    .in_1(adder_1_out), .out_2(l_32to31_82463699_3_out_2), .out_3(l_32to31_82463699_3_out_3));
  xor xor_1 (xor_1_out, l_32to31_82463699_3_out_3, l_32to31_82463699_1_out_3);
  xor xor_2 (xor_2_out, xor_1_out, l_32to31_82463699_2_out_3);
  L_31to32_3c6b2aeb l_31to32_3c6b2aeb_3 (.in_1(l_32to31_82463699_3_out_2), .in_2(xor_2_out), .out_3(Result));
  add_new_sign add_new_sign_1 (.in_1(A), .in_2(B), .out_3(Overflow));
endmodule

module add_new_sign (
  input  [31:0] in_1,
  input  [31:0] in_2,
  output out_3
);

  wire and_1_out, and_2_out, and_3_out, and_4_out, and_5_out, and_7_out, and_8_out, and_9_out, and_10_out,
       and_11_out, comparator_1_eq, comparator_1_gt, comparator_1_lt, comparator_2_eq, comparator_2_gt,
       comparator_2_lt, l_32to31_82463699_1_out_3, l_32to31_82463699_2_out_3, not_1_out, not_2_out, undriven,
       undriven_2;
  wire [30:0] l_32to31_82463699_1_out_2, l_32to31_82463699_2_out_2;
  wire [31:0] adder2_1_out_3, adder2_2_out_3, l_31to32_3c6b2aeb_1_out_3, l_31to32_3c6b2aeb_2_out_3,
       negator_1_out, negator_2_out, sele_32_1_out_3, sele_32_2_out_3, sele_32_3_out_3, sele_32_4_out_3;

  L_32to31_82463699 l_32to31_82463699_1 (
    .in_1(in_2), .out_2(l_32to31_82463699_1_out_2), .out_3(l_32to31_82463699_1_out_3));
  L_31to32_3c6b2aeb l_31to32_3c6b2aeb_1 (
    .in_1(l_32to31_82463699_1_out_2), .in_2(l_32to31_82463699_1_out_3), .out_3(l_31to32_3c6b2aeb_1_out_3));
  L_32to31_82463699 l_32to31_82463699_2 (
    .in_1(in_1), .out_2(l_32to31_82463699_2_out_2), .out_3(l_32to31_82463699_2_out_3));
  L_31to32_3c6b2aeb l_31to32_3c6b2aeb_2 (
    .in_1(l_32to31_82463699_2_out_2), .in_2(l_32to31_82463699_2_out_3), .out_3(l_31to32_3c6b2aeb_2_out_3));
  Negator #(.width(32)) negator_1 (.in(l_31to32_3c6b2aeb_2_out_3), .out(negator_1_out));
  Negator #(.width(32)) negator_2 (.in(l_31to32_3c6b2aeb_1_out_3), .out(negator_2_out));
  not not_1 (not_1_out, l_32to31_82463699_2_out_3);
  not not_2 (not_2_out, l_32to31_82463699_1_out_3);
  Sele_32 sele_32_1 (.in_1(l_31to32_3c6b2aeb_2_out_3), .in_2(not_1_out), .out_3(sele_32_1_out_3));
  Sele_32 sele_32_2 (.in_1(negator_1_out), .in_2(l_32to31_82463699_2_out_3), .out_3(sele_32_2_out_3));
  Sele_32 sele_32_3 (.in_1(l_31to32_3c6b2aeb_1_out_3), .in_2(not_2_out), .out_3(sele_32_3_out_3));
  Sele_32 sele_32_4 (.in_1(negator_2_out), .in_2(l_32to31_82463699_1_out_3), .out_3(sele_32_4_out_3));
  Adder2 adder2_1 (.in_1(sele_32_1_out_3), .in_2(sele_32_2_out_3), .out_3(adder2_1_out_3));  // open: out_4
  Adder2 adder2_2 (.in_1(sele_32_3_out_3), .in_2(sele_32_4_out_3), .out_3(adder2_2_out_3));  // open: out_4
  Comparator #(.mode("unsigned"), .width(32)) comparator_1 (
    .a(adder2_1_out_3), .b(adder2_2_out_3), .gt(comparator_1_gt), .eq(comparator_1_eq), .lt(comparator_1_lt));
  Comparator #(.width(32)) comparator_2 (
    .a(in_1), .b(in_2), .gt(comparator_2_gt), .eq(comparator_2_eq), .lt(comparator_2_lt));
  and and_1 (and_1_out, comparator_1_gt, comparator_2_gt);
  and and_2 (and_2_out, comparator_1_lt, comparator_2_lt);
  and and_3 (and_3_out, comparator_1_lt, comparator_2_gt);
  and and_4 (and_4_out, comparator_1_gt, comparator_2_lt);
  and and_5 (and_5_out, undriven, comparator_2_eq);
  // AND_Gate and_6 has open pins: in0=undriven_2, in1=comparator_1_eq, out=open
  and and_7 (and_7_out, and_2_out, l_32to31_82463699_1_out_3);
  and and_8 (and_8_out, and_5_out, l_32to31_82463699_2_out_3);
  and and_9 (and_9_out, and_1_out, l_32to31_82463699_2_out_3);
  and and_10 (and_10_out, and_3_out, l_32to31_82463699_2_out_3);
  and and_11 (and_11_out, and_4_out, l_32to31_82463699_1_out_3);
  or or_1 (out_3, and_9_out, and_7_out, and_10_out, and_11_out, and_8_out);
endmodule

module mulhu (
  input  [31:0] A,
  input  [31:0] B,
  output [31:0] Result
);

  wire [31:0] adder_1_out, multiplier_1_out, multiplier_2_out, multiplier_3_out;

  Multiplier #(.width(32)) multiplier_1 (
    .a({{16{1'b0}}, A[15:0]}), .b({{16{1'b0}}, B[31:16]}), .out(multiplier_1_out));  // open: cin, cout
  Multiplier #(.width(32)) multiplier_2 (
    .a({{16{1'b0}}, A[31:16]}), .b({{16{1'b0}}, B[15:0]}), .out(multiplier_2_out));  // open: cin, cout
  Multiplier #(.width(32)) multiplier_3 (
    .a({{16{1'b0}}, A[31:16]}), .b({{16{1'b0}}, B[31:16]}), .out(multiplier_3_out));  // open: cin, cout
  Adder #(.width(32)) adder_1 (.a(multiplier_1_out), .b(multiplier_2_out), .out(adder_1_out));  // open: cin, cout
  Adder #(.width(32)) adder_2 (.a(adder_1_out), .b(multiplier_3_out), .out(Result));  // open: cin, cout
endmodule

module add4th (
  input  [31:0] in_1,
  input  [31:0] in_2,
  output [31:0] out_3,
  output out_4
);

  Adder #(.width(32)) adder_1 (.a(in_1), .b(in_2), .out(out_3), .cout(out_4));  // open: cin
endmodule

module sltu (
  input  [31:0] in_1,
  input  [31:0] in_2,
  output [31:0] out_3
);

  wire comparator_1_eq, comparator_1_gt, comparator_1_lt, not_1_out, not_2_out;

  Comparator #(.mode("unsigned"), .width(32)) comparator_1 (
    .a(in_1), .b(in_2), .gt(comparator_1_gt), .eq(comparator_1_eq), .lt(comparator_1_lt));
  not not_1 (not_1_out, comparator_1_gt);
  not not_2 (not_2_out, comparator_1_eq);
  and and_1 (out_3[0], not_1_out, not_2_out, comparator_1_lt);

  assign out_3[31:1] = {31{1'b0}};
endmodule
