// Logisim project processor_4.circ as structural Verilog
module main (
  input  clock,
  input  ResetMemoryCounter,
  input  ResetRegisters,
  input  [4:0] Registerselect,
  output [31:0] RegisterOutput
);

  wire and_1_out, controlunit_1_alusrc, controlunit_1_branch, controlunit_1_memread, controlunit_1_memtoreg,
       controlunit_1_memwrite, controlunit_1_regwrite, main2_1_zero;
  wire [3:0] alucontrol_1_alusel;
  wire [4:0] rom_1_data_2;
  wire [6:0] rom_1_data_3;
  wire [7:0] main2_1_result;
  wire [11:0] adder_1_out, adder_2_out, immgen_1_out_3, multiplexer_1_out, multiplexer_2_out,
       ProgramCounter_q;
  wire [31:0] immgen_1_out_2, multiplexer_3_out, multiplexer_4_out, ram_1_dout, regfile_1_readdata1,
       regfile_1_readdata2;
  wire [31:8] main2_1_result_2;
  wire [31:12] rom_1_data;

  Register #(.width(12)) ProgramCounter (
    .D(multiplexer_1_out), .en(1'b1), .clk(clock), .Q(ProgramCounter_q));  // open: clr
  Multiplexer #(.width(12)) multiplexer_1 (
    .in0(multiplexer_2_out), .in1({12{1'b0}}), .out(multiplexer_1_out), .sel(ResetMemoryCounter));
  ROM #(.addrWidth(12), .dataWidth(32)) rom_1 (
    .addr(ProgramCounter_q), .data({rom_1_data, rom_1_data_2, rom_1_data_3}));
  Adder #(.width(12)) adder_1 (.a(ProgramCounter_q), .b(12'h1), .out(adder_1_out));  // open: cin, cout
  Adder #(.width(12)) adder_2 (.a(ProgramCounter_q), .b(immgen_1_out_3), .out(adder_2_out));  // open: cin, cout
  ControlUnit controlunit_1 (
    .in_1(rom_1_data_3), .Branch(controlunit_1_branch), .MemWrite(controlunit_1_memwrite),
    .MemRead(controlunit_1_memread), .RegWrite(controlunit_1_regwrite), .MemtoReg(controlunit_1_memtoreg),
    .ALUsrc(controlunit_1_alusrc));  // open: ALUOp0, ALUOp1
  ImmGen immgen_1 (
    .Instruction({rom_1_data, rom_1_data_2, rom_1_data_3}), .out_2(immgen_1_out_2), .out_3(immgen_1_out_3));
  Multiplexer #(.width(12)) multiplexer_2 (
    .in0(adder_1_out), .in1(adder_2_out), .out(multiplexer_2_out), .sel(and_1_out));
  and and_1 (and_1_out, controlunit_1_branch, main2_1_zero);
  ALUcontrol alucontrol_1 (.Instruction({rom_1_data, rom_1_data_2, rom_1_data_3}), .ALUsel(alucontrol_1_alusel));
  RegFile regfile_1 (
    .RegWEn(controlunit_1_regwrite), .rs1(rom_1_data[19:15]), .rs2(rom_1_data[24:20]), .rd(rom_1_data_2),
    .WriteData(multiplexer_4_out), .clock(clock), .in_7(Registerselect), .Reset(ResetRegisters),
    .ReadData1(regfile_1_readdata1), .ReadData2(regfile_1_readdata2), .out_11(RegisterOutput));
  Multiplexer #(.width(32)) multiplexer_3 (
    .in0(regfile_1_readdata2), .in1(immgen_1_out_2), .out(multiplexer_3_out), .sel(controlunit_1_alusrc));
  main2 main2_1 (
    .ALUSel(alucontrol_1_alusel), .A(multiplexer_3_out), .B(regfile_1_readdata1),
    .Result({main2_1_result_2, main2_1_result}), .Zero(main2_1_zero));  // open: OverFlow
  RAM #(.asyncread("true"), .dataWidth(32)) ram_1 (
    .addr(main2_1_result), .we(controlunit_1_memwrite), .oe(controlunit_1_memread), .clk(clock),
    .din(regfile_1_readdata2), .dout(ram_1_dout));
  Multiplexer #(.width(32)) multiplexer_4 (
    .in0({main2_1_result_2, main2_1_result}), .in1(ram_1_dout), .out(multiplexer_4_out),
    .sel(controlunit_1_memtoreg));

  // Notes on the sheet:
  //   contents of rom_1 (hex, n*v repeats v):
  //   2300293 2900313 1300393 7302b3 407302b3 63e2b3 62f4b3 6294b3 64d2b3 64a2b3 733333
endmodule

module RegFile (
  input  RegWEn,
  input  [4:0] rs1,
  input  [4:0] rs2,
  input  [4:0] rd,
  input  [31:0] WriteData,
  input  clock,
  input  [4:0] in_7,
  input  Reset,
  output [31:0] ReadData1,
  output [31:0] ReadData2,
  output [31:0] out_11
);

  wire and_1_out, and_2_out, and_3_out, and_4_out, and_5_out, and_6_out, and_7_out, and_8_out, and_9_out,
       and_10_out, and_11_out, and_12_out, and_13_out, and_14_out, and_15_out, and_16_out, not_1_out,
       not_2_out, not_3_out, not_4_out, not_5_out, not_6_out, not_7_out, not_8_out, not_9_out, not_10_out,
       not_11_out, not_12_out, not_13_out, not_14_out, not_15_out, not_16_out, not_17_out, not_18_out,
       not_19_out, not_20_out, not_21_out, not_22_out, not_23_out, not_24_out, not_25_out, not_26_out,
       or_1_out, or_2_out, or_3_out, or_4_out, or_5_out, or_6_out, or_7_out, or_8_out;
  wire [31:0] multiplexer_1_out, x0_q, x1_q, x2_q, x5_q, x6_q, x7_q, x8_q, x9_q, x10_q;

  Multiplexer #(.width(32)) multiplexer_1 (.in0(WriteData), .in1({32{1'b0}}), .out(multiplexer_1_out), .sel(Reset));
  not not_1 (not_1_out, rd[1]);
  not not_2 (not_2_out, rd[2]);
  not not_3 (not_3_out, rd[3]);
  not not_4 (not_4_out, rd[4]);
  not not_5 (not_5_out, rd[0]);
  not not_6 (not_6_out, rd[2]);
  not not_7 (not_7_out, rd[3]);
  not not_8 (not_8_out, rd[4]);
  not not_9 (not_9_out, rd[1]);
  not not_10 (not_10_out, rd[3]);
  not not_11 (not_11_out, rd[4]);
  not not_12 (not_12_out, rd[0]);
  not not_13 (not_13_out, rd[3]);
  not not_14 (not_14_out, rd[4]);
  not not_15 (not_15_out, rd[3]);
  not not_16 (not_16_out, rd[4]);
  not not_17 (not_17_out, rd[1]);
  not not_18 (not_18_out, rd[2]);
  not not_19 (not_19_out, rd[4]);
  not not_20 (not_20_out, rd[1]);
  not not_21 (not_21_out, rd[2]);
  not not_22 (not_22_out, rd[4]);
  not not_23 (not_23_out, rd[2]);
  not not_24 (not_24_out, rd[4]);
  not not_25 (not_25_out, rd[0]);
  not not_26 (not_26_out, rd[0]);
  and and_1 (and_1_out, rd[0], not_1_out, not_2_out, not_3_out, not_4_out);
  and and_2 (and_2_out, not_5_out, rd[1], not_6_out, not_7_out, not_8_out);
  and and_3 (and_3_out, rd[0], not_9_out, rd[2], not_10_out, not_11_out);
  and and_4 (and_4_out, not_12_out, rd[1], rd[2], not_13_out, not_14_out);
  and and_5 (and_5_out, rd[0], rd[1], rd[2], not_15_out, not_16_out);
  and and_6 (and_6_out, not_25_out, not_17_out, not_18_out, rd[3], not_19_out);
  and and_7 (and_7_out, rd[0], not_20_out, not_21_out, rd[3], not_22_out);
  and and_8 (and_8_out, not_26_out, rd[1], not_23_out, rd[3], not_24_out);
  and and_9 (and_9_out, RegWEn, and_1_out);
  and and_10 (and_10_out, RegWEn, and_2_out);
  and and_11 (and_11_out, RegWEn, and_3_out);
  and and_12 (and_12_out, RegWEn, and_4_out);
  and and_13 (and_13_out, RegWEn, and_5_out);
  and and_14 (and_14_out, RegWEn, and_6_out);
  and and_15 (and_15_out, RegWEn, and_7_out);
  and and_16 (and_16_out, RegWEn, and_8_out);
  or or_1 (or_1_out, and_9_out, Reset);
  or or_2 (or_2_out, and_10_out, Reset);
  or or_3 (or_3_out, and_11_out, Reset);
  or or_4 (or_4_out, and_12_out, Reset);
  or or_5 (or_5_out, and_13_out, Reset);
  or or_6 (or_6_out, and_14_out, Reset);
  or or_7 (or_7_out, and_15_out, Reset);
  or or_8 (or_8_out, and_16_out, Reset);
  Register #(.width(32)) x0 (.D({32{1'b0}}), .clk(clock), .Q(x0_q));  // open: en, clr
  Register #(.width(32)) x2 (.D(multiplexer_1_out), .en(or_2_out), .clk(clock), .Q(x2_q));  // open: clr
  Register #(.width(32)) x5 (.D(multiplexer_1_out), .en(or_3_out), .clk(clock), .Q(x5_q));  // open: clr
  Register #(.width(32)) x6 (.D(multiplexer_1_out), .en(or_4_out), .clk(clock), .Q(x6_q));  // open: clr
  Register #(.width(32)) x8 (.D(multiplexer_1_out), .en(or_6_out), .clk(clock), .Q(x8_q));  // open: clr
  Register #(.width(32)) x9 (.D(multiplexer_1_out), .en(or_7_out), .clk(clock), .Q(x9_q));  // open: clr
  Register #(.width(32)) x10 (.D(multiplexer_1_out), .en(or_8_out), .clk(clock), .Q(x10_q));  // open: clr
  Register #(.width(32)) x1 (.D(multiplexer_1_out), .en(or_1_out), .clk(clock), .Q(x1_q));  // open: clr
  Register #(.width(32)) x7 (.D(multiplexer_1_out), .en(or_5_out), .clk(clock), .Q(x7_q));  // open: clr
  Multiplexer #(.enable("true"), .select(5), .width(32)) multiplexer_2 (
    .in0(x0_q), .in1(x1_q), .in2(x2_q), .in5(x5_q), .in6(x6_q), .in7(x7_q), .in8(x8_q), .in9(x9_q),
    .in10(x10_q), .out(ReadData1), .sel(rs1));  // open: in3, in4, in11, in12, in13, in14, in15, in16, in17, in18, in19, in20, in21, in22, in23, in24, in25, in26, in27, in28, in29, in30, in31, en
  Multiplexer #(.enable("true"), .select(5), .width(32)) multiplexer_3 (
    .in0(x0_q), .in1(x1_q), .in2(x2_q), .in5(x5_q), .in6(x6_q), .in7(x7_q), .in8(x8_q), .in9(x9_q),
    .in10(x10_q), .out(ReadData2), .sel(rs2));  // open: in3, in4, in11, in12, in13, in14, in15, in16, in17, in18, in19, in20, in21, in22, in23, in24, in25, in26, in27, in28, in29, in30, in31, en
  Multiplexer #(.enable("true"), .select(5), .width(32)) multiplexer_4 (
    .in0(x0_q), .in1(x1_q), .in2(x2_q), .in5(x5_q), .in6(x6_q), .in7(x7_q), .in8(x8_q), .in9(x9_q),
    .in10(x10_q), .out(out_11), .sel(in_7));  // open: in3, in4, in11, in12, in13, in14, in15, in16, in17, in18, in19, in20, in21, in22, in23, in24, in25, in26, in27, in28, in29, in30, in31, en
endmodule

module Decoder_4 (
  input  [31:0] in_1
);

  wire not_1_out, not_2_out, not_3_out, not_4_out, not_5_out, not_6_out, not_7_out, not_8_out, not_9_out,
       not_10_out, not_11_out, not_12_out, not_13_out, not_14_out, not_15_out, not_16_out, not_17_out,
       not_18_out, not_19_out, not_20_out, not_21_out, not_22_out, not_23_out, not_24_out, not_25_out,
       not_26_out, not_27_out, not_28_out;
  wire [6:0] undriven;

  not not_1 (not_1_out, undriven[0]);
  not not_2 (not_2_out, undriven[1]);
  not not_3 (not_3_out, undriven[2]);
  not not_4 (not_4_out, undriven[3]);
  not not_5 (not_5_out, undriven[4]);
  not not_6 (not_6_out, undriven[5]);
  not not_7 (not_7_out, undriven[6]);
  not not_8 (not_8_out, undriven[0]);
  not not_9 (not_9_out, undriven[1]);
  not not_10 (not_10_out, undriven[2]);
  not not_11 (not_11_out, undriven[3]);
  not not_12 (not_12_out, undriven[4]);
  not not_13 (not_13_out, undriven[5]);
  not not_14 (not_14_out, undriven[6]);
  not not_15 (not_15_out, undriven[0]);
  not not_16 (not_16_out, undriven[1]);
  not not_17 (not_17_out, undriven[2]);
  not not_18 (not_18_out, undriven[3]);
  not not_19 (not_19_out, undriven[4]);
  not not_20 (not_20_out, undriven[5]);
  not not_21 (not_21_out, undriven[6]);
  not not_22 (not_22_out, undriven[0]);
  not not_23 (not_23_out, undriven[1]);
  not not_24 (not_24_out, undriven[2]);
  not not_25 (not_25_out, undriven[3]);
  not not_26 (not_26_out, undriven[4]);
  not not_27 (not_27_out, undriven[5]);
  not not_28 (not_28_out, undriven[6]);
  // AND_Gate and_1 has open pins: in0=not_1_out, in1=not_2_out, in2=not_3_out, in3=not_4_out, in4=not_5_out, in5=not_6_out, in6=not_7_out, out=open
  // AND_Gate and_2 has open pins: in0=not_8_out, in1=not_9_out, in2=not_10_out, in3=not_11_out, in4=not_12_out, in5=not_13_out, in6=not_14_out, out=open
  // AND_Gate and_3 has open pins: in0=not_15_out, in1=not_16_out, in2=not_17_out, in3=not_18_out, in4=not_19_out, in5=not_20_out, in6=not_21_out, out=open
  // AND_Gate and_4 has open pins: in0=not_22_out, in1=not_23_out, in2=not_24_out, in3=not_25_out, in4=not_26_out, in5=not_27_out, in6=not_28_out, out=open
endmodule

module ControlUnit (
  input  [6:0] in_1,
  output ALUOp0,
  output ALUOp1,
  output Branch,
  output MemWrite,
  output MemRead,
  output RegWrite,
  output MemtoReg,
  output ALUsrc
);

  wire beq_out, I_out, lw_out, not_1_out, not_2_out, not_3_out, not_4_out, not_5_out, not_6_out, not_7_out,
       not_8_out, not_9_out, not_10_out, not_11_out, not_12_out, not_13_out, not_14_out, not_15_out,
       not_16_out, not_17_out, not_18_out, not_19_out, R_out, sw_out;
  wire [2:0] encoder_1_out_8;

  not not_1 (not_1_out, in_1[2]);
  not not_2 (not_2_out, in_1[3]);
  not not_3 (not_3_out, in_1[6]);
  not not_4 (not_4_out, in_1[2]);
  not not_5 (not_5_out, in_1[3]);
  not not_6 (not_6_out, in_1[5]);
  not not_7 (not_7_out, in_1[6]);
  not not_8 (not_8_out, in_1[2]);
  not not_9 (not_9_out, in_1[3]);
  not not_10 (not_10_out, in_1[4]);
  not not_11 (not_11_out, in_1[5]);
  not not_12 (not_12_out, in_1[6]);
  not not_13 (not_13_out, in_1[2]);
  not not_14 (not_14_out, in_1[3]);
  not not_15 (not_15_out, in_1[4]);
  not not_16 (not_16_out, in_1[6]);
  not not_17 (not_17_out, in_1[2]);
  not not_18 (not_18_out, in_1[3]);
  not not_19 (not_19_out, in_1[4]);
  and R (R_out, in_1[0], in_1[1], not_1_out, not_2_out, in_1[4], in_1[5], not_3_out);
  and I (I_out, in_1[0], in_1[1], not_4_out, not_5_out, in_1[4], not_6_out, not_7_out);
  and lw (lw_out, in_1[0], in_1[1], not_8_out, not_9_out, not_10_out, not_11_out, not_12_out);
  and sw (sw_out, in_1[0], in_1[1], not_13_out, not_14_out, not_15_out, in_1[5], not_16_out);
  and beq (beq_out, in_1[0], in_1[1], not_17_out, not_18_out, not_19_out, in_1[5], in_1[6]);
  Multiplexer #(.select(3), .width(8)) multiplexer_1 (
    .in0({8{1'b0}}), .in1(8'h44), .in2(8'h45), .in3(8'hf), .in4(8'h11), .in5(8'ha0), .in6({8{1'b0}}),
    .in7({8{1'b0}}), .out({ALUOp0, ALUOp1, Branch, MemWrite, MemRead, RegWrite, MemtoReg, ALUsrc}),
    .sel(encoder_1_out_8));
  Encoder encoder_1 (
    .in_1(1'b0), .in_2(1'b0), .in_3(beq_out), .in_4(sw_out), .in_5(lw_out), .in_6(I_out), .in_7(R_out),
    .out_8(encoder_1_out_8));
endmodule

module Encoder (
  input  in_1,
  input  in_2,
  input  in_3,
  input  in_4,
  input  in_5,
  input  in_6,
  input  in_7,
  output [2:0] out_8
);

  or or_1 (out_8[2], in_1, in_2, in_3, in_4);
  or or_2 (out_8[1], in_1, in_2, in_5, in_6);
  or or_3 (out_8[0], in_1, in_3, in_5, in_7);
endmodule

module Processor (
  input  clock,
  input  ResetMemoryCounter,
  input  ResetRegisters,
  input  [4:0] Registerselect,
  output [31:0] RegisterOutput
);

  wire and_1_out, controlunit_1_alusrc, controlunit_1_branch, controlunit_1_memread, controlunit_1_memtoreg,
       controlunit_1_memwrite, controlunit_1_regwrite, main2_1_zero, undriven;
  wire [3:0] alucontrol_1_alusel;
  wire [4:0] rom_1_data_2;
  wire [6:0] rom_1_data_3;
  wire [7:0] main2_1_result;
  wire [11:0] adder_1_out, adder_2_out, immgen_1_out_3, multiplexer_1_out, multiplexer_2_out,
       ProgramCounter_q;
  wire [31:0] immgen_1_out_2, multiplexer_3_out, multiplexer_4_out, ram_1_dout, regfile_1_readdata1,
       regfile_1_readdata2;
  wire [31:8] main2_1_result_2;
  wire [31:12] rom_1_data;

  Register #(.width(12)) ProgramCounter (
    .D(multiplexer_1_out), .en(1'b1), .clk(clock), .Q(ProgramCounter_q));  // open: clr
  Multiplexer #(.width(12)) multiplexer_1 (
    .in0(multiplexer_2_out), .in1({12{1'b0}}), .out(multiplexer_1_out), .sel(ResetMemoryCounter));
  ROM #(.addrWidth(12), .dataWidth(32)) rom_1 (
    .addr(ProgramCounter_q), .data({rom_1_data, rom_1_data_2, rom_1_data_3}));
  Adder #(.width(12)) adder_1 (.a(ProgramCounter_q), .b(12'h1), .out(adder_1_out));  // open: cin, cout
  Adder #(.width(12)) adder_2 (.a(ProgramCounter_q), .b(immgen_1_out_3), .out(adder_2_out));  // open: cin, cout
  ControlUnit controlunit_1 (
    .in_1(rom_1_data_3), .Branch(controlunit_1_branch), .MemWrite(controlunit_1_memwrite),
    .MemRead(controlunit_1_memread), .RegWrite(controlunit_1_regwrite), .MemtoReg(controlunit_1_memtoreg),
    .ALUsrc(controlunit_1_alusrc));  // open: ALUOp0, ALUOp1
  ImmGen immgen_1 (
    .Instruction({rom_1_data, rom_1_data_2, rom_1_data_3}), .out_2(immgen_1_out_2), .out_3(immgen_1_out_3));
  Multiplexer #(.width(12)) multiplexer_2 (
    .in0(adder_1_out), .in1(adder_2_out), .out(multiplexer_2_out), .sel(and_1_out));
  and and_1 (and_1_out, controlunit_1_branch, main2_1_zero);
  ALUcontrol alucontrol_1 (.Instruction({rom_1_data, rom_1_data_2, rom_1_data_3}), .ALUsel(alucontrol_1_alusel));
  RegFile regfile_1 (
    .RegWEn(controlunit_1_regwrite), .rs1(rom_1_data[19:15]), .rs2(rom_1_data[24:20]), .rd(rom_1_data_2),
    .WriteData(multiplexer_4_out), .clock(clock), .in_7(Registerselect), .Reset(undriven),
    .ReadData1(regfile_1_readdata1), .ReadData2(regfile_1_readdata2), .out_11(RegisterOutput));
  Multiplexer #(.width(32)) multiplexer_3 (
    .in0(regfile_1_readdata2), .in1(immgen_1_out_2), .out(multiplexer_3_out), .sel(controlunit_1_alusrc));
  main2 main2_1 (
    .ALUSel(alucontrol_1_alusel), .A(multiplexer_3_out), .B(regfile_1_readdata1),
    .Result({main2_1_result_2, main2_1_result}), .Zero(main2_1_zero));  // open: OverFlow
  RAM #(.asyncread("true"), .dataWidth(32)) ram_1 (
    .addr(main2_1_result), .we(controlunit_1_memwrite), .oe(controlunit_1_memread), .clk(clock),
    .din(regfile_1_readdata2), .dout(ram_1_dout));
  Multiplexer #(.width(32)) multiplexer_4 (
    .in0({main2_1_result_2, main2_1_result}), .in1(ram_1_dout), .out(multiplexer_4_out),
    .sel(controlunit_1_memtoreg));

  // Notes on the sheet:
  //   contents of rom_1 (hex, n*v repeats v):
  //   1338393 f30313 638333 602223 402283 100263 fe100fe3 0 0 fe100fe3
endmodule

module ALUcontrol (
  input  [31:0] Instruction,
  output [3:0] ALUsel
);

  wire beq_out, lw_out, not_1_out, not_2_out, not_3_out, not_4_out, not_5_out, not_6_out, not_7_out,
       not_8_out, not_9_out, not_10_out, not_11_out, not_12_out, sw_out;
  wire [2:0] encoder_1_out_8;
  wire [3:0] multiplexer_1_out;

  Multiplexer #(.width(4)) multiplexer_1 (
    .in0({1'b0, Instruction[13:11]}), .in1(4'b1100), .out(multiplexer_1_out), .sel(Instruction[30]));
  not not_1 (not_1_out, Instruction[2]);
  not not_2 (not_2_out, Instruction[3]);
  not not_3 (not_3_out, Instruction[4]);
  not not_4 (not_4_out, Instruction[5]);
  not not_5 (not_5_out, Instruction[6]);
  not not_6 (not_6_out, Instruction[2]);
  not not_7 (not_7_out, Instruction[3]);
  not not_8 (not_8_out, Instruction[4]);
  not not_9 (not_9_out, Instruction[6]);
  not not_10 (not_10_out, Instruction[2]);
  not not_11 (not_11_out, Instruction[3]);
  not not_12 (not_12_out, Instruction[4]);
  and lw (lw_out, Instruction[0], Instruction[1], not_1_out, not_2_out, not_3_out, not_4_out, not_5_out);
  and sw (sw_out, Instruction[0], Instruction[1], not_6_out, not_7_out, not_8_out, Instruction[5], not_9_out);
  and beq (beq_out, Instruction[0], Instruction[1], not_10_out, not_11_out, not_12_out, Instruction[5], Instruction[6]);
  Encoder encoder_1 (
    .in_1(1'b0), .in_2(1'b0), .in_3(1'b0), .in_4(1'b0), .in_5(beq_out), .in_6(sw_out), .in_7(lw_out),
    .out_8(encoder_1_out_8));
  Multiplexer #(.select(3), .width(4)) multiplexer_2 (
    .in0(multiplexer_1_out), .in1(4'b0000), .in2(4'b0000), .in3(4'b1100), .in4(4'b0000), .in5(4'b0000),
    .in6(4'b0000), .in7(4'b0000), .out(ALUsel), .sel(encoder_1_out_8));
endmodule

module ImmGen (
  input  [31:0] Instruction,
  output [31:0] out_2,
  output [11:0] out_3
);

  wire beq_out, I_out, lw_out, not_1_out, not_2_out, not_3_out, not_4_out, not_5_out, not_6_out, not_7_out,
       not_8_out, not_9_out, not_10_out, not_11_out, not_12_out, not_13_out, not_14_out, not_15_out,
       not_16_out, or_1_out, sw_out;
  wire [2:0] encoder_1_out_8;
  wire [31:0] bit_extender_1_out, bit_extender_2_out, bit_extender_3_out;

  not not_1 (not_1_out, Instruction[2]);
  not not_2 (not_2_out, Instruction[3]);
  not not_3 (not_3_out, Instruction[5]);
  not not_4 (not_4_out, Instruction[6]);
  not not_5 (not_5_out, Instruction[2]);
  not not_6 (not_6_out, Instruction[3]);
  not not_7 (not_7_out, Instruction[4]);
  not not_8 (not_8_out, Instruction[5]);
  not not_9 (not_9_out, Instruction[6]);
  not not_10 (not_10_out, Instruction[2]);
  not not_11 (not_11_out, Instruction[3]);
  not not_12 (not_12_out, Instruction[4]);
  not not_13 (not_13_out, Instruction[6]);
  not not_14 (not_14_out, Instruction[2]);
  not not_15 (not_15_out, Instruction[3]);
  not not_16 (not_16_out, Instruction[4]);
  and I (I_out, Instruction[0], Instruction[1], not_1_out, not_2_out, Instruction[4], not_3_out, not_4_out);
  and lw (lw_out, Instruction[0], Instruction[1], not_5_out, not_6_out, not_7_out, not_8_out, not_9_out);
  and sw (sw_out, Instruction[0], Instruction[1], not_10_out, not_11_out, not_12_out, Instruction[5], not_13_out);
  and beq (beq_out, Instruction[0], Instruction[1], not_14_out, not_15_out, not_16_out, Instruction[5], Instruction[6]);
  or or_1 (or_1_out, I_out, lw_out);
  Encoder encoder_1 (
    .in_1(1'b0), .in_2(1'b0), .in_3(1'b0), .in_4(1'b0), .in_5(beq_out), .in_6(sw_out), .in_7(or_1_out),
    .out_8(encoder_1_out_8));
  assign bit_extender_1_out = {{20{Instruction[31]}}, Instruction[31:20]};  // Bit_Extender bit_extender_1
  assign bit_extender_2_out = {{19{Instruction[31]}}, {Instruction[31], Instruction[7], Instruction[30:25], Instruction[11:8], 1'b0}};  // Bit_Extender bit_extender_2
  assign bit_extender_3_out = {{20{Instruction[31]}}, {Instruction[31:25], Instruction[11:7]}};  // Bit_Extender bit_extender_3
  Multiplexer #(.select(3), .width(32)) multiplexer_1 (
    .in0({32{1'b0}}), .in1(bit_extender_1_out), .in2(bit_extender_3_out), .in3(bit_extender_2_out),
    .in4({32{1'b0}}), .in5({32{1'b0}}), .in6({32{1'b0}}), .in7({32{1'b0}}), .out(out_2), .sel(encoder_1_out_8));
  Bit_Extender #(.in_width(32), .out_width(12)) bit_extender_4 (.in(out_2), .out(out_3));
endmodule
